# Fritzing sketch circuit (saved by Fritzing 0.9.1b)

parts:
  Raspberry_Pi1 = Raspberry Pi B+
  RGB_SMD_LED1 = SMD RGB LED (WS2812) [package=5050]
  S1 = Toggle Switch [package=THT]
  U1 = Voltage Regulator - 5V [package="DPak [SMD]"]

nets:
  N1: Raspberry_Pi1.GPIO18, RGB_SMD_LED1.DIn
  N2: Raspberry_Pi1.GND, RGB_SMD_LED1.DOut, S1.L2
  5V: Raspberry_Pi1.5V, RGB_SMD_LED1.VCC, U1.output_voltage
  N3: S1.COM, U1.GND
